// Logisim project y86.circ as structural Verilog: 14 circuits, main circuit main
module main (
  input  Reset
);

  wire and_1_out, and_2_out, Clock_out, Cnd, dmem_err, imem_err, instr_valid_instr_valid, needReg_needreg,
       needValC_needvalc, nor_1_out, not_1_out, setCC_setcc;
  wire [1:0] setStat_stat, Stat_q;
  wire [2:0] CC, CCHold_q;
  wire [3:0] dstE, dstM, icode, ifun, rA, rB, srcA, srcB;
  wire [7:0] imem_p4, imem_p5, imem_p6, imem_p7, imem_p8, imem_p9, imem_p10, imem_p11, imem_p12;
  wire [31:0] newPC, PC, PC_q, valA_0, valA_1, valB_0, valB_1, valC_0, valC_1, valE_0, valE_1, valM_0,
       valM_1, valP_0, valP_1;

  needValC needValC (.icode(icode), .needValC(needValC_needvalc));
  and and_1 (and_1_out, Clock_out, nor_1_out);
  Clock Clock (.out(Clock_out));
  Register #(.width(32)) u_PC (.D(PC), .Q(PC_q), .clk(and_1_out), .clr(Reset));  // open: en
  PCincrement PCi (.needValC(needValC_needvalc), .PC(PC), .needReg(needReg_needreg), .valP_1(valP_1), .valP_0(valP_0));
  nor nor_1 (nor_1_out, Stat_q[1], Stat_q[0]);
  aluAB aluab_1 (
    .valC_1(valC_1), .valC_0(valC_0), .valA_1(valA_1), .valA_0(valA_0), .valB_1(valB_1), .valB_0(valB_0),
    .icode(icode));  // open: aluA_1, aluA_0, aluB_1, aluB_0
  // alu alu: pin names not known; wires that end beside it: valE_1, valE_0
  ALUfun alufun_1 (.icode(icode), .ifun(ifun));  // open: ALUfun
  // imem imem: pin names not known; wires that end beside it: PC_q, imem_err, {icode, ifun}, imem_p4, imem_p5, imem_p6, imem_p7, imem_p8, imem_p9, imem_p10, imem_p11, imem_p12
  not not_1 (not_1_out, and_1_out);
  Register #(.width(2)) Stat (.D(setStat_stat), .Q(Stat_q), .clk(not_1_out), .clr(Reset));  // open: en
  Align align (
    .B1(imem_p4), .B2(imem_p5), .B3(imem_p6), .B4(imem_p7), .B5(imem_p8), .B6(imem_p9), .B7(imem_p10),
    .B8(imem_p11), .B9(imem_p12), .NeedRegs(needReg_needreg), .rA(rA), .rB(rB), .valC_1(valC_1),
    .valC_0(valC_0));
  needReg needReg (.needReg(needReg_needreg), .icode(icode));
  instr_valid instr_valid (.icode(icode), .instr_valid(instr_valid_instr_valid));
  Stat setStat (
    .dmem_err(dmem_err), .imem_err(imem_err), .instr_valid(instr_valid_instr_valid), .icode(icode),
    .Stat(setStat_stat));
  // ABEM ABEM: pin names not known; wires that end beside it: rA, rB, valE_1, valE_0, valM_1, valM_0, icode, srcA, Cnd, srcB, dstM, dstE, not_1_out, Reset, valA_1, valA_0, valB_1, valB_0
  // regfile regfile_1: pin names not known
  newPC u_newPC (
    .valC_1(valC_1), .valC_0(valC_0), .valM_1(valM_1), .valM_0(valM_0), .valP_1(valP_1), .valP_0(valP_0),
    .icode(icode), .Cnd(Cnd), .newPC(newPC));
  and and_2 (and_2_out, not_1_out, setCC_setcc);
  mCtrl mCtrl (
    .valE_1(valE_1), .valE_0(valE_0), .valA_1(valA_1), .valA_0(valA_0), .valP_1(valP_1), .valP_0(valP_0),
    .icode(icode));  // open: addr_1, addr_0, data_1, data_0, read, write
  CCC CCC (.CCSaved(CCHold_q), .ifun(ifun), .Cnd(Cnd));
  Register #(.width(3)) CCHold (.D(CC), .Q(CCHold_q), .clk(and_2_out), .clr(Reset));  // open: en
  setCC setCC (.icode(icode), .setCC(setCC_setcc));
  // dmem dmem_1: pin names not known; wires that end beside it: dmem_err, not_1_out, valM_1, valM_0
  Register #(.width(32)) PChold (.D(newPC), .Q(PC), .clk(not_1_out), .clr(Reset));  // open: en
  // Probe on ifun
  // Probe on icode
  // Probe on valA_1
  // Probe on valE_1
  // Probe on valC_1
  // Probe on rA
  // Probe on valA_0
  // Probe on valE_0
  // Probe on valC_0
  // Probe on rB
  // Probe on srcA
  // Probe on valB_1
  // Probe on valM_1
  // Probe on valP_0
  // Probe on srcB
  // Probe on valB_0
  // Probe on valM_0
  // Probe on PC
  // Probe on dstM
  // Probe on CC
  // Probe on newPC
  // Probe on dstE
endmodule

module Align (
  input  [7:0] B1,
  input  [7:0] B2,
  input  [7:0] B3,
  input  [7:0] B4,
  input  [7:0] B5,
  input  [7:0] B6,
  input  [7:0] B7,
  input  [7:0] B8,
  input  [7:0] B9,
  input  NeedRegs,
  output [3:0] rA,
  output [3:0] rB,
  output [31:0] valC_1,
  output [31:0] valC_0
);

  Multiplexer #(.width(32), .enable("false")) multiplexer_1 (
    .in0({B4, B3, B2, B1}), .in1({B5, B4, B3, B2}), .out(valC_0), .sel(NeedRegs));
  Multiplexer #(.width(32), .enable("false")) multiplexer_2 (
    .in0({B8, B7, B6, B5}), .in1({B9, B8, B7, B6}), .out(valC_1), .sel(NeedRegs));

  assign rA = B1[7:4];
  assign rB = B1[3:0];
endmodule

module needReg (
  input  [3:0] icode,
  output needReg
);

  Multiplexer #(.select(4), .enable("false")) multiplexer_1 (
    .in0(1'b0), .in1(1'b0), .in2(1'b1), .in3(1'b1), .in4(1'b1), .in5(1'b1), .in6(1'b1), .in7(1'b0),
    .in8(1'b0), .in9(1'b0), .in10(1'b1), .in11(1'b1), .in12(1'b0), .in13(1'b0), .in14(1'b0), .in15(1'b0),
    .out(needReg), .sel(icode));
endmodule

module aluAB (
  input  [31:0] valC_1,
  input  [31:0] valC_0,
  input  [31:0] valA_1,
  input  [31:0] valA_0,
  input  [31:0] valB_1,
  input  [31:0] valB_0,
  input  [3:0] icode,
  output [31:0] aluA_1,
  output [31:0] aluA_0,
  output [31:0] aluB_1,
  output [31:0] aluB_0
);

  Multiplexer #(.select(4), .width(32), .enable("false")) multiplexer_1 (
    .in0({32{1'b1}}), .in1({32{1'b1}}), .in2(valA_1), .in3(valC_1), .in4(valC_1), .in5(valC_1), .in6(valA_1),
    .in7({32{1'b1}}), .in8({32{1'b1}}), .in9({32{1'b0}}), .in10({32{1'b1}}), .in11({32{1'b0}}),
    .in12({32{1'b1}}), .in13({32{1'b1}}), .in14({32{1'b1}}), .in15({32{1'b1}}), .out(aluA_1), .sel(icode));
  Multiplexer #(.select(4), .width(32), .enable("false")) multiplexer_2 (
    .in0({32{1'b1}}), .in1({32{1'b1}}), .in2(valA_0), .in3(valC_0), .in4(valC_0), .in5(valC_0), .in6(valA_0),
    .in7({32{1'b1}}), .in8(32'hfffffff8), .in9(32'h8), .in10(32'hfffffff8), .in11(32'h8), .in12({32{1'b1}}),
    .in13({32{1'b1}}), .in14({32{1'b1}}), .in15({32{1'b1}}), .out(aluA_0), .sel(icode));
  Multiplexer #(.select(4), .width(32), .enable("false")) multiplexer_3 (
    .in0({32{1'b1}}), .in1({32{1'b1}}), .in2({32{1'b0}}), .in3({32{1'b0}}), .in4(valB_1), .in5(valB_1),
    .in6(valB_1), .in7({32{1'b1}}), .in8(valB_1), .in9(valB_1), .in10(valB_1), .in11(valB_1), .in12(valB_1),
    .in13(valB_1), .in14(valB_1), .in15(valB_1), .out(aluB_1), .sel(icode));
  Multiplexer #(.select(4), .width(32), .enable("false")) multiplexer_4 (
    .in0(valB_1), .in1(valB_1), .in2({32{1'b0}}), .in3({32{1'b0}}), .in4(valB_0), .in5(valB_0), .in6(valB_0),
    .in7(valB_1), .in8(valB_0), .in9(valB_0), .in10(valB_0), .in11(valB_0), .in12(valB_1), .in13(valB_1),
    .in14(valB_1), .in15(valB_1), .out(aluB_0), .sel(icode));
endmodule

module ABEM (
  input  [3:0] rA,
  input  [3:0] rB,
  input  Cnd,
  input  [31:0] valE_1,
  input  [31:0] valE_0,
  input  [31:0] valM_1,
  input  [31:0] valM_0,
  input  [3:0] icode,
  output [3:0] srcA,
  output [3:0] srcA_2,
  output [3:0] srcB,
  output [3:0] srcB_2,
  output [3:0] dstE,
  output [31:0] valE_1_2,
  output [3:0] dstE_2,
  output [31:0] valE_0_2,
  output [3:0] dstM,
  output [3:0] dstM_2,
  output [31:0] valM_1_2,
  output [31:0] valM_0_2
);

  wire [1:1] multiplexer_5_out;
  wire [3:0] multiplexer_3_out;

  Multiplexer #(.select(4), .width(4), .enable("false")) multiplexer_1 (
    .in0(4'b1111), .in1(4'b1111), .in2(rA), .in3(4'b1111), .in4(rA), .in5(4'b1111), .in6(rA), .in7(4'b1111),
    .in8(4'b1111), .in9(4'b0100), .in10(rA), .in11(4'b0100), .in12(4'b1111), .in13(4'b1111), .in14(4'b1111),
    .in15(4'b1111), .out(srcA), .sel(icode));
  Multiplexer #(.select(4), .width(4), .enable("false")) multiplexer_2 (
    .in0(4'b1111), .in1(4'b1111), .in2(4'b1111), .in3(4'b1111), .in4(rB), .in5(rB), .in6(rB), .in7(4'b1111),
    .in8(4'b0100), .in9(4'b0100), .in10(4'b0100), .in11(4'b0100), .in12(4'b1111), .in13(4'b1111),
    .in14(4'b1111), .in15(4'b1111), .out(srcB), .sel(icode));
  Multiplexer #(.select(4), .width(4), .enable("false")) multiplexer_3 (
    .in0(4'b1111), .in1(4'b1111), .in2(rB), .in3(rB), .in4(4'b1111), .in5(4'b1111), .in6(rB), .in7(4'b1111),
    .in8(4'b0100), .in9(4'b0100), .in10(4'b0100), .in11(4'b0100), .in12(4'b1111), .in13(4'b1111),
    .in14(4'b1111), .in15(4'b1111), .out(multiplexer_3_out), .sel(icode));
  Multiplexer #(.select(4), .width(4), .enable("false")) multiplexer_4 (
    .in0(4'b1111), .in1(4'b1111), .in2(4'b1111), .in3(4'b1111), .in4(4'b1111), .in5(rA), .in6(4'b1111),
    .in7(4'b1111), .in8(4'b1111), .in9(4'b1111), .in10(4'b1111), .in11(rA), .in12(4'b1111), .in13(4'b1111),
    .in14(4'b1111), .in15(4'b1111), .out(dstM), .sel(icode));
  Multiplexer #(.select(4), .enable("false")) multiplexer_5 (
    .in0(1'b0), .in1(1'b0), .in2(1'b1), .in3(1'b0), .in4(1'b0), .in5(1'b0), .in6(1'b0), .in7(1'b0),
    .in8(1'b0), .in9(1'b0), .in10(1'b0), .in11(1'b0), .in12(1'b0), .in13(1'b0), .in14(1'b0), .in15(1'b0),
    .out(multiplexer_5_out[1]), .sel(icode));
  Multiplexer #(.select(2), .width(4), .enable("false")) multiplexer_6 (
    .in0(multiplexer_3_out), .in1(multiplexer_3_out), .in2(4'b1111), .in3(multiplexer_3_out), .out(dstE),
    .sel({multiplexer_5_out[1], Cnd}));

  assign dstE_2 = dstE;
  assign dstM_2 = dstM;
  assign srcA_2 = srcA;
  assign srcB_2 = srcB;
  assign valE_0_2 = valE_0;
  assign valE_1_2 = valE_1;
  assign valM_0_2 = valM_0;
  assign valM_1_2 = valM_1;
endmodule

module mCtrl (
  input  [31:0] valE_1,
  input  [31:0] valE_0,
  input  [31:0] valA_1,
  input  [31:0] valA_0,
  input  [31:0] valP_1,
  input  [31:0] valP_0,
  input  [3:0] icode,
  output [31:0] addr_1,
  output [31:0] addr_0,
  output [31:0] data_1,
  output [31:0] data_0,
  output read,
  output write
);

  Multiplexer #(.select(4), .width(32), .enable("false")) multiplexer_1 (
    .in0({32{1'b0}}), .in1({32{1'b0}}), .in2({32{1'b0}}), .in3({32{1'b0}}), .in4(valE_1), .in5(valE_1),
    .in6({32{1'b0}}), .in7({32{1'b0}}), .in8(valE_1), .in9(valA_1), .in10(valE_1), .in11(valA_1),
    .in12({32{1'b0}}), .in13(valP_0), .in14(valP_0), .in15(valP_0), .out(addr_1), .sel(icode));
  Multiplexer #(.select(4), .width(32), .enable("false")) multiplexer_2 (
    .in0({32{1'b0}}), .in1({32{1'b0}}), .in2({32{1'b0}}), .in3({32{1'b0}}), .in4(valE_0), .in5(valE_0),
    .in6({32{1'b0}}), .in7({32{1'b0}}), .in8(valE_0), .in9(valA_0), .in10(valE_0), .in11(valA_0),
    .in12({32{1'b0}}), .in13(valP_0), .in14(valP_0), .in15(valP_0), .out(addr_0), .sel(icode));
  Multiplexer #(.select(4), .width(32), .enable("false")) multiplexer_3 (
    .in0({32{1'b0}}), .in1({32{1'b0}}), .in2({32{1'b0}}), .in3({32{1'b0}}), .in4(valA_1), .in5({32{1'b0}}),
    .in6({32{1'b0}}), .in7({32{1'b0}}), .in8(valP_1), .in9({32{1'b0}}), .in10(valA_1), .in11({32{1'b0}}),
    .in12({32{1'b0}}), .in13(valP_0), .in14(valP_0), .in15(valP_0), .out(data_1), .sel(icode));
  Multiplexer #(.select(4), .width(32), .enable("false")) multiplexer_4 (
    .in0({32{1'b0}}), .in1({32{1'b0}}), .in2({32{1'b0}}), .in3({32{1'b0}}), .in4(valA_0), .in5({32{1'b0}}),
    .in6({32{1'b0}}), .in7({32{1'b0}}), .in8(valP_0), .in9({32{1'b0}}), .in10(valA_0), .in11({32{1'b0}}),
    .in12({32{1'b0}}), .in13({32{1'b0}}), .in14({32{1'b0}}), .in15({32{1'b0}}), .out(data_0), .sel(icode));
  Multiplexer #(.select(4), .enable("false")) multiplexer_5 (
    .in0(1'b0), .in1(1'b0), .in2(1'b0), .in3(1'b0), .in4(1'b0), .in5(1'b1), .in6(1'b0), .in7(1'b0),
    .in8(1'b0), .in9(1'b1), .in10(1'b0), .in11(1'b1), .in12(1'b0), .in13(1'b0), .in14(1'b0), .in15(1'b0),
    .out(read), .sel(icode));
  Multiplexer #(.select(4), .enable("false")) multiplexer_6 (
    .in0(1'b0), .in1(1'b0), .in2(1'b0), .in3(1'b0), .in4(1'b1), .in5(1'b0), .in6(1'b0), .in7(1'b0),
    .in8(1'b1), .in9(1'b0), .in10(1'b1), .in11(1'b0), .in12(1'b0), .in13(1'b0), .in14(1'b0), .in15(1'b0),
    .out(write), .sel(icode));
endmodule

module newPC (
  input  [31:0] valC_1,
  input  [31:0] valC_0,
  input  [31:0] valM_1,
  input  [31:0] valM_0,
  input  [31:0] valP_1,
  input  [31:0] valP_0,
  input  Cnd,
  input  [3:0] icode,
  output [31:0] newPC
);

  wire [31:0] multiplexer_3_out, multiplexer_4_out;

  Multiplexer #(.select(4), .width(32), .enable("false")) multiplexer_1 (
    .in0(valP_1), .in1(valP_1), .in2(valP_1), .in3(valP_1), .in4(valP_1), .in5(valP_1), .in6(valP_1),
    .in7(multiplexer_3_out), .in8(valC_1), .in9(valM_1), .in10(valP_1), .in11(valP_1), .in12(valP_1),
    .in13(valP_1), .in14(valP_1), .in15(valP_1), .sel(icode));  // open: out
  Multiplexer #(.select(4), .width(32), .enable("false")) multiplexer_2 (
    .in0(valP_0), .in1(valP_0), .in2(valP_0), .in3(valP_0), .in4(valP_0), .in5(valP_0), .in6(valP_0),
    .in7(multiplexer_4_out), .in8(valC_0), .in9(valM_0), .in10(valP_0), .in11(valP_0), .in12(valP_0),
    .in13(valP_0), .in14(valP_0), .in15(valP_0), .out(newPC), .sel(icode));
  Multiplexer #(.width(32), .enable("false")) multiplexer_3 (
    .in0(valP_1), .in1(valC_1), .out(multiplexer_3_out), .sel(Cnd));
  Multiplexer #(.width(32), .enable("false")) multiplexer_4 (
    .in0(valP_0), .in1(valC_0), .out(multiplexer_4_out), .sel(Cnd));
endmodule

module CCC (
  input  [2:0] CCSaved,
  input  [3:0] ifun,
  output Cnd
);

  wire jg_out, jge_out, jl_out, jle_out, jne_out, not_1_out, not_2_out, xor_1_out, xor_2_out, xor_3_out;

  xor xor_1 (xor_1_out, CCSaved[1], CCSaved[0]);
  xor jl (jl_out, CCSaved[1], CCSaved[0]);
  not jne (jne_out, CCSaved[2]);
  xor xor_2 (xor_2_out, CCSaved[1], CCSaved[0]);
  not jge (jge_out, xor_2_out);
  xor xor_3 (xor_3_out, CCSaved[1], CCSaved[0]);
  not not_1 (not_1_out, xor_3_out);
  not not_2 (not_2_out, CCSaved[2]);
  or jle (jle_out, xor_1_out, CCSaved[2]);
  and jg (jg_out, not_1_out, not_2_out);
  Multiplexer #(.select(4), .enable("false")) multiplexer_1 (
    .in0(1'b1), .in1(jle_out), .in2(jl_out), .in3(CCSaved[2]), .in4(jne_out), .in5(jge_out), .in6(jg_out),
    .out(Cnd), .sel(ifun));  // open: in7, in8, in9, in10, in11, in12, in13, in14, in15
endmodule

module PCincrement (
  input  [31:0] PC,
  input  needValC,
  input  needReg,
  output [31:0] valP_1,
  output [31:0] valP_0
);

  wire [31:0] adder_1_out, adder_2_out, adder_3_out, adder_4_out;

  Adder #(.width(32)) adder_1 (.a(PC), .b(32'h1), .out(adder_1_out));  // open: cin, cout
  Adder #(.width(32)) adder_2 (.a(PC), .b(32'h9), .out(adder_2_out));  // open: cin, cout
  Adder #(.width(32)) adder_3 (.a(PC), .b(32'h2), .out(adder_3_out));  // open: cin, cout
  Adder #(.width(32)) adder_4 (.a(PC), .b(32'ha), .out(adder_4_out));  // open: cin, cout
  Multiplexer #(.select(2), .width(32), .enable("false")) multiplexer_1 (
    .in0(adder_1_out), .in1(adder_2_out), .in2(adder_3_out), .in3(adder_4_out), .out(valP_0),
    .sel({needReg, needValC}));

  assign valP_1 = {32{1'b0}};
endmodule

module Stat (
  input  [3:0] icode,
  input  dmem_err,
  input  imem_err,
  input  instr_valid,
  output [1:0] Stat
);

  wire not_1_out, not_2_out, not_3_out, not_4_out, not_5_out, not_6_out, or_1_out;
  wire [3:0] multiplexer_1_out;

  Multiplexer #(.select(4), .enable("false")) multiplexer_1 (
    .in0(1'b1), .in1(1'b0), .in2(1'b0), .in3(1'b0), .in4(1'b0), .in5(1'b0), .in6(1'b0), .in7(1'b0),
    .in8(1'b0), .in9(1'b0), .in10(1'b0), .in11(1'b0), .in12(1'b0), .in13(1'b0), .in14(1'b0), .in15(1'b0),
    .out(multiplexer_1_out[0]), .sel(icode));
  or or_1 (or_1_out, dmem_err, imem_err);
  not not_1 (not_1_out, multiplexer_1_out[0]);
  not not_2 (not_2_out, instr_valid);
  not not_3 (not_3_out, multiplexer_1_out[0]);
  not not_4 (not_4_out, multiplexer_1_out[0]);
  not not_5 (not_5_out, or_1_out);
  not not_6 (not_6_out, instr_valid);
  and and_1 (multiplexer_1_out[1], not_1_out, or_1_out, not_2_out);
  and and_2 (multiplexer_1_out[2], not_3_out, instr_valid);
  and and_3 (multiplexer_1_out[3], not_4_out, not_5_out, not_6_out);
  Multiplexer #(.select(4), .width(2), .enable("false")) multiplexer_2 (
    .in1(2'b11), .in2(2'b10), .in4(2'b01), .in8(2'b00), .out(Stat), .sel(multiplexer_1_out));  // open: in0, in3, in5, in6, in7, in9, in10, in11, in12, in13, in14, in15
  // Probe on multiplexer_1_out
endmodule

module ALUfun (
  input  [3:0] ifun,
  input  [3:0] icode,
  output [3:0] ALUfun
);

  Multiplexer #(.select(4), .width(4), .enable("false")) multiplexer_1 (
    .in0(4'b0000), .in1(4'b0000), .in2(4'b0000), .in3(4'b0000), .in4(4'b0000), .in5(4'b0000), .in6(ifun),
    .in7(ifun), .in8(4'b0000), .in9(4'b0000), .in10(4'b0000), .in11(4'b0000), .in12(4'b0000), .in13(4'b0000),
    .in14(4'b0000), .in15(4'b0000), .out(ALUfun), .sel(icode));
endmodule

module needValC (
  input  [3:0] icode,
  output needValC
);

  Multiplexer #(.select(4), .enable("false")) multiplexer_1 (
    .in0(1'b0), .in1(1'b0), .in2(1'b0), .in3(1'b1), .in4(1'b1), .in5(1'b1), .in6(1'b0), .in7(1'b1),
    .in8(1'b1), .in9(1'b0), .in10(1'b0), .in11(1'b0), .in12(1'b0), .in13(1'b0), .in14(1'b0), .in15(1'b0),
    .out(needValC), .sel(icode));
endmodule

module instr_valid (
  input  [3:0] icode,
  output instr_valid
);

  Multiplexer #(.select(4), .enable("false")) multiplexer_1 (
    .in0(1'b0), .in1(1'b0), .in2(1'b0), .in3(1'b0), .in4(1'b0), .in5(1'b0), .in6(1'b0), .in7(1'b0),
    .in8(1'b0), .in9(1'b0), .in10(1'b0), .in11(1'b0), .in12(1'b1), .in13(1'b1), .in14(1'b1), .in15(1'b1),
    .out(instr_valid), .sel(icode));
endmodule

module setCC (
  input  [3:0] icode,
  output setCC
);

  Multiplexer #(.select(4), .enable("false")) multiplexer_1 (
    .in0(1'b0), .in1(1'b0), .in2(1'b0), .in3(1'b0), .in4(1'b0), .in5(1'b0), .in6(1'b1), .in7(1'b0),
    .in8(1'b0), .in9(1'b0), .in10(1'b0), .in11(1'b0), .in12(1'b0), .in13(1'b0), .in14(1'b0), .in15(1'b0),
    .out(setCC), .sel(icode));
endmodule
